# Fritzing sketch Schema2 (saved by Fritzing 0.9.3b)
stripboards: 1

parts:
  part = Basic Servo
  Pulsante = Pushbutton [package="[SMD]"]
  part_2 = Digispark

nets:
  GND: part.gnd, part_2.GND
  VCC: part.vcc, Pulsante.Pin_1, Pulsante.Pin_2, part_2.VCC
  N1: part.pulse, part_2.P3
  N2: Pulsante.Pin_3, Pulsante.Pin_4, part_2.P2

custom parts:
  Digispark: The Digispark is an Attiny85 based microcontroller development board similar to the Arduino line, only cheaper, smaller, and a bit less powerful. With a whole host of shields to extend its functionality and the ability to use the familiar Arduino IDE the Digispark is a great way to jump into electronics, or perfect for when an Arduino is too big or too much.
