# Fritzing sketch Schema1 (saved by Fritzing 0.9.3b)
stripboards: 1

parts:
  LED1 = LED - 5mm [color="Red (633nm)" package="5 mm [THT]"]
  Digispark1 = Digispark
  R2 = Resistor [tolerance=±5% resistance=180 package="1206 [SMD]"]
  R3 = Trimmer Potentiometer [maximum_resistance=10kΩ package=THT]

nets:
  N1: LED1.cathode, R2.Pin_0
  N2: LED1.anode, Digispark1.P0
  N3: Digispark1.VCC, R3.leg1
  N4: Digispark1.GND, R2.Pin_1, R3.leg2
  N5: Digispark1.P2, R3.wiper

custom parts:
  Digispark: The Digispark is an Attiny85 based microcontroller development board similar to the Arduino line, only cheaper, smaller, and a bit less powerful. With a whole host of shields to extend its functionality and the ability to use the familiar Arduino IDE the Digispark is a great way to jump into electronics, or perfect for when an Arduino is too big or too much.
