# Fritzing sketch Schema3 (saved by Fritzing 0.9.3b)
stripboards: 1

parts:
  Digispark2 = Digispark
  LED = smd LED [color="Red (633nm)" package="1206 [SMD]"]
  Ultrasuoni = hc-sr04

nets:
  VCC: Digispark2.VCC, Ultrasuoni.VCC
  GND: Digispark2.GND, LED.cathode, Ultrasuoni.GND
  N1: Digispark2.P0, LED.anode
  N2: Digispark2.P2, Ultrasuoni.Echo
  N3: Digispark2.P3, Ultrasuoni.Trig

custom parts:
  Digispark: The Digispark is an Attiny85 based microcontroller development board similar to the Arduino line, only cheaper, smaller, and a bit less powerful. With a whole host of shields to extend its functionality and the ability to use the familiar Arduino IDE the Digispark is a great way to jump into electronics, or perfect for when an Arduino is too big or too much.
