# Fritzing sketch Schema1 (saved by Fritzing 0.9.3b)
stripboards: 1

parts:
  R1 = Trimmer Potentiometer [maximum_resistance=10kΩ package=THT]
  LED1 = LED - 5mm [color="Red (633nm)" package="5 mm [THT]"]
  R2 = Resistor [tolerance=±5% resistance=330 package=THT]
  Digispark1 = Digispark

nets:
  N1: R1.leg1, R1.wiper, LED1.anode, Digispark1.P5
  N2: R1.leg2, R2.Pin_0, Digispark1.GND
  N3: LED1.cathode, R2.Pin_1

custom parts:
  Digispark: The Digispark is an Attiny85 based microcontroller development board similar to the Arduino line, only cheaper, smaller, and a bit less powerful. With a whole host of shields to extend its functionality and the ability to use the familiar Arduino IDE the Digispark is a great way to jump into electronics, or perfect for when an Arduino is too big or too much.
